// Logisim project e86.circ as structural Verilog: 12 circuits, main circuit main
module main (
);

  wire clock_1_out, Reset_out;
  wire [7:0] rom_1_p2, rom_1_p3, rom_1_p4, rom_1_p5, rom_1_p6, rom_1_p7, rom_1_p8, rom_1_p9;
  wire [15:0] bit_extender_1_out;
  wire [63:0] cpu_1_memaddress;

  Clock clock_1 (.out(clock_1_out));
  Button Reset (.out(Reset_out));
  CPU cpu_1 (
    .MemDataIn({rom_1_p9, rom_1_p8, rom_1_p7, rom_1_p6, rom_1_p5, rom_1_p4, rom_1_p3, rom_1_p2}),
    .Clock(clock_1_out), .Reset(Reset_out), .MemAddress(cpu_1_memaddress));  // open: MemData, MemEnable, MemWrite, MemSize
  Bit_Extender #(.in_width(64), .\type ("zero")) bit_extender_1 (.in(cpu_1_memaddress), .out(bit_extender_1_out));
  // ROM #(.addrWidth(16), .line("octo"), .misaligned("true")) rom_1: pin names not known; wires that end beside it: bit_extender_1_out, rom_1_p2, rom_1_p3, rom_1_p4, rom_1_p5, rom_1_p6, rom_1_p7, rom_1_p8, rom_1_p9
endmodule

module CPU (
  input  [63:0] MemDataIn,
  input  Clock,
  input  Reset,
  output [63:0] MemAddress,
  output [63:0] MemData,
  output MemEnable,
  output MemWrite,
  output [1:0] MemSize
);

  wire aludriver_1_readflags, aludriver_1_writeflags, and_1_out, Latch, MemEnable_t, MemWrite_t, not_1_out,
       not_2_out, NotWriteRIP, or_1_out, OverrideALU, OverrideFlags, PretendFetch, RegWrite, State_qn,
       StateExec, StateFetch, StateReset;
  wire [1:0] Cycle, FlagsMode, FlagsOverride, ImmediateMode, microcode_1_dstmode, microcode_1_src0mode,
       microcode_1_src1mode, Scale, Size;
  wire [2:0] RegSrc;
  wire [4:0] Dst, instructiondecoder_1_a, instructiondecoder_1_b, instructiondecoder_1_d, Src0, Src1;
  wire [5:0] aludriver_1_aluop, ALUOp, ALUOverride;
  wire [7:0] Opcode;
  wire [63:0] Address, alu_1_i, alu_1_o, aludriver_1_a, aludriver_1_b, Flags, Immediate, Instruction_q,
       instructiondecoder_1_instructionsize, multiplexer_1_out, multiplexer_2_out, multiplexer_3_out, NewRIP,
       Reg0, regfile_1_read1data, RIP;

  RegFile regfile_1 (
    .WriteReg(Dst), .WriteEnable(RegWrite), .Data(multiplexer_2_out), .Read0Reg(Src0), .Read1Reg(Src1),
    .RIPOverride(StateFetch), .RIPData(NewRIP), .Clock(Clock), .Reset(Reset), .Read0Data(Reg0),
    .Read1Data(regfile_1_read1data), .RIP(RIP));
  Register #(.width(64)) Instruction (.D(MemDataIn), .en(StateFetch), .clk(Clock), .Q(Instruction_q));  // open: clr
  and and_1 (and_1_out, StateReset, ~PretendFetch);  // AND_Gate
  Microcode microcode_1 (
    .Enable(StateExec), .Opcode(Opcode), .Src0Mode(microcode_1_src0mode), .Src1Mode(microcode_1_src1mode),
    .DstMode(microcode_1_dstmode), .MemEnable(MemEnable_t), .MemWrite(MemWrite_t), .AddressLatch(Latch),
    .RegWrite(RegWrite), .ImmediateMode(ImmediateMode), .OverrideALU(OverrideALU), .ALUOverride(ALUOverride),
    .OverrideFlags(OverrideFlags), .FlagsOverride(FlagsOverride), .StateReset(StateReset), .RegSrc(RegSrc));  // open: Cycle
  not not_1 (not_1_out, RegWrite);
  not not_2 (not_2_out, MemEnable_t);
  S_R_Flip_Flop State (
    .S(StateFetch), .R(and_1_out), .clk(Clock), .Q(StateExec), .reset(Reset), .Qn(State_qn));  // open: preset
  or or_1 (or_1_out, not_1_out, NotWriteRIP);
  AddressUnit addressunit_1 (
    .Base(Reg0), .Index(regfile_1_read1data), .Immediate(Immediate), .Scale(Scale), .Latch(Latch),
    .Clock(Clock), .Address(Address));
  Multiplexer #(.width(64)) multiplexer_1 (
    .in0(Instruction_q), .in1(MemDataIn), .out(multiplexer_1_out), .sel(StateFetch));
  and and_2 (PretendFetch, not_2_out, StateReset, or_1_out);
  Multiplexer #(.select(3), .width(64)) multiplexer_2 (
    .in0(alu_1_o), .in1(MemDataIn), .in2(Address), .out(multiplexer_2_out), .sel(RegSrc));  // open: in3, in4, in5, in6, in7
  ALUDriver aludriver_1 (
    .InstructionALUOp(ALUOp), .InstructionFlagsMode(FlagsMode), .Reg0(Reg0), .Reg1(regfile_1_read1data),
    .Immediate(Immediate), .Mode(ImmediateMode), .OverrideALU(OverrideALU), .ALUOverrideValue(ALUOverride),
    .OverrideFlagsMode(OverrideFlags), .FlagsModeOverride(FlagsOverride), .ALUOp(aludriver_1_aluop),
    .A(aludriver_1_a), .B(aludriver_1_b), .WriteFlags(aludriver_1_writeflags),
    .ReadFlags(aludriver_1_readflags));
  Multiplexer #(.disabled("Z"), .width(64)) multiplexer_3 (
    .in0({64{1'b0}}), .in1(Flags), .out(multiplexer_3_out), .sel(aludriver_1_readflags));
  ALU alu_1 (
    .Op(aludriver_1_aluop), .A(aludriver_1_a), .B(aludriver_1_b), .C(multiplexer_3_out), .O(alu_1_o),
    .I(alu_1_i));
  Counter #(.max('h3), .width(2)) counter_1 (
    .clr(Reset), .load(StateFetch), .up(1'b1), .count(1'b1), .clk(Clock), .D(2'b00), .Q(Cycle));  // open: carry
  or or_2 (StateFetch, State_qn, PretendFetch);
  Register #(.width(64)) u_Flags (.D(alu_1_i), .en(aludriver_1_writeflags), .clk(Clock), .Q(Flags));  // open: clr
  InstructionDecoder instructiondecoder_1 (
    .InstructionWord(multiplexer_1_out), .InstructionSize(instructiondecoder_1_instructionsize),
    .Opcode(Opcode), .A(instructiondecoder_1_a), .B(instructiondecoder_1_b), .D(instructiondecoder_1_d),
    .ALUOp(ALUOp), .FlagsMode(FlagsMode), .Immediate(Immediate), .Scale(Scale), .Size(Size));
  Adder #(.width(64)) adder_1 (
    .a(RIP), .b(instructiondecoder_1_instructionsize), .out(NewRIP), .cin(1'b0));  // open: cout
  Multiplexer #(.width(64)) multiplexer_4 (.in0(Address), .in1(RIP), .out(MemAddress), .sel(StateFetch));
  Multiplexer #(.width(2)) multiplexer_5 (.in0(Size), .in1(2'b11), .out(MemSize), .sel(StateFetch));
  assign MemData = MemWrite ? Reg0 : 64'bz;  // Controlled_Buffer controlled_buffer_1
  or or_3 (MemEnable, MemEnable_t, StateFetch);
  and and_3 (MemWrite, ~StateFetch, MemWrite_t);  // AND_Gate
  RegDriver regdriver_1 (
    .A(instructiondecoder_1_a), .B(instructiondecoder_1_b), .D(instructiondecoder_1_d),
    .Src0Mode(microcode_1_src0mode), .Src1Mode(microcode_1_src1mode), .DstMode(microcode_1_dstmode),
    .Src0(Src0), .Src1(Src1), .Dst(Dst));
  nand nand_1 (NotWriteRIP, Dst[0], Dst[1], Dst[2], Dst[3], Dst[4]);
endmodule

module ALU (
  input  [5:0] Op,
  input  [63:0] A,
  input  [63:0] B,
  input  [63:0] C,
  output [63:0] O,
  output [63:0] I
);

  wire adder_1_cout, comparator_1_eq, comparator_1_gt, comparator_1_lt, comparator_2_gt, comparator_2_lt,
       comparator_3_eq, comparator_3_lt, comparator_4_eq, Family0, Family1, Family2, Family3, Family4,
       Family5, Family6, multiplexer_2_out, multiplexer_3_out, multiplexer_5_out, not_2_out, not_3_out,
       not_4_out, not_5_out, not_6_out, not_7_out, not_8_out, not_9_out, subtractor_1_bout;
  wire [5:0] bit_extender_4_out;
  wire [63:0] adder_1_out, and_1_out, bit_extender_1_out, bit_extender_2_out, bit_extender_3_out,
       bit_extender_5_out, bit_extender_6_out, multiplexer_8_out, multiplier_1_cout, multiplier_1_out,
       multiplier_2_cout, multiplier_2_out, negator_1_out, not_1_out, or_1_out, or_2_out, shifter_1_out,
       shifter_2_out, shifter_3_out, shifter_4_out, subtractor_1_out, xor_1_out;

  assign O = Family4 ? bit_extender_1_out : 64'bz;  // Controlled_Buffer controlled_buffer_1
  assign I = Family4 ? bit_extender_1_out : 64'bz;  // Controlled_Buffer controlled_buffer_2
  assign O = Family5 ? bit_extender_2_out : 64'bz;  // Controlled_Buffer controlled_buffer_3
  assign I = Family5 ? bit_extender_2_out : 64'bz;  // Controlled_Buffer controlled_buffer_4
  Multiplexer #(.disabled("Z"), .enable("true"), .select(3), .width(64)) multiplexer_1 (
    .in0(not_1_out), .in1(negator_1_out), .out(O), .sel(Op[2:0]), .en(Family0));  // open: in2, in3, in4, in5, in6, in7
  assign not_1_out = ~A;  // NOT_Gate not_1, 64 bits wide
  assign bit_extender_1_out = {{63{1'b0}}, multiplexer_2_out};  // Bit_Extender bit_extender_1
  Multiplexer #(.disabled("Z"), .select(3)) multiplexer_2 (
    .in0(comparator_1_gt), .in1(comparator_1_lt), .in2(comparator_2_gt), .in3(comparator_2_lt),
    .in4(not_2_out), .in5(not_3_out), .in6(not_4_out), .in7(not_5_out), .out(multiplexer_2_out), .sel(Op[2:0]));
  assign bit_extender_2_out = {{63{1'b0}}, multiplexer_3_out};  // Bit_Extender bit_extender_2
  Multiplexer #(.disabled("Z"), .select(3)) multiplexer_3 (
    .in0(comparator_1_eq), .in1(not_6_out), .out(multiplexer_3_out), .sel(Op[2:0]));  // open: in2, in3, in4, in5, in6, in7
  Negator #(.width(64)) negator_1 (.in(A), .out(negator_1_out));
  Comparator #(.width(64)) comparator_1 (
    .a(A), .b(B), .gt(comparator_1_gt), .eq(comparator_1_eq), .lt(comparator_1_lt));
  Comparator #(.mode("unsigned"), .width(64)) comparator_2 (
    .a(A), .b(B), .gt(comparator_2_gt), .lt(comparator_2_lt));  // open: eq
  not not_2 (not_2_out, comparator_1_gt);
  not not_3 (not_3_out, comparator_1_lt);
  not not_4 (not_4_out, comparator_2_gt);
  not not_5 (not_5_out, comparator_2_lt);
  not not_6 (not_6_out, comparator_1_eq);
  Decoder #(.enable("false"), .select(3)) decoder_1 (
    .out0(Family0), .out1(Family1), .out2(Family2), .out3(Family3), .out4(Family4), .out5(Family5),
    .out6(Family6), .sel(Op[5:3]));  // open: out7
  Multiplexer #(.disabled("Z"), .enable("true"), .select(3), .width(64)) multiplexer_4 (
    .in0(and_1_out), .in1(or_1_out), .in2(xor_1_out), .in3(shifter_1_out), .in4(shifter_2_out),
    .in5(shifter_3_out), .in6(or_2_out), .out(O), .sel(Op[2:0]), .en(Family1));  // open: in7
  assign and_1_out = B & A;  // AND_Gate and_1, 64 bits wide
  assign O = Family3 ? bit_extender_3_out : 64'bz;  // Controlled_Buffer controlled_buffer_5
  assign or_1_out = B | A;  // OR_Gate or_1, 64 bits wide
  assign I = Family3 ? bit_extender_3_out : 64'bz;  // Controlled_Buffer controlled_buffer_6
  assign xor_1_out = B ^ A;  // XOR_Gate xor_1, 64 bits wide
  assign bit_extender_3_out = {{63{1'b0}}, multiplexer_5_out};  // Bit_Extender bit_extender_3
  Multiplexer #(.disabled("Z"), .select(3)) multiplexer_5 (
    .in0(comparator_3_eq), .in1(not_7_out), .in2(comparator_3_lt), .in3(not_8_out), .out(multiplexer_5_out),
    .sel(Op[2:0]));  // open: in4, in5, in6, in7
  Bit_Extender #(.in_width(64), .out_width(6)) bit_extender_4 (.in(B), .out(bit_extender_4_out));
  Comparator #(.width(64)) comparator_3 (
    .a(A), .b({64{1'b0}}), .eq(comparator_3_eq), .lt(comparator_3_lt));  // open: gt
  Shifter #(.width(64)) shifter_1 (.in(A), .\dist (bit_extender_4_out), .out(shifter_1_out));
  Shifter #(.shift("lr"), .width(64)) shifter_2 (.in(A), .\dist (bit_extender_4_out), .out(shifter_2_out));
  Shifter #(.shift("ar"), .width(64)) shifter_3 (.in(A), .\dist (bit_extender_4_out), .out(shifter_3_out));
  not not_7 (not_7_out, comparator_3_eq);
  not not_8 (not_8_out, comparator_3_lt);
  Shifter #(.width(64)) shifter_4 (.in(A), .\dist (6'b100000), .out(shifter_4_out));
  assign or_2_out = shifter_4_out | B;  // OR_Gate or_2, 64 bits wide
  Multiplexer #(.disabled("Z"), .enable("true"), .select(3), .width(64)) multiplexer_6 (
    .in0(adder_1_out), .in1(subtractor_1_out), .in2(multiplier_1_out), .in3(multiplier_2_out),
    .in4(multiplexer_8_out), .out(O), .sel(Op[2:0]), .en(Family2));  // open: in5, in6, in7
  Comparator #(.mode("unsigned"), .width(64)) comparator_4 (
    .a(C), .b({64{1'b0}}), .eq(comparator_4_eq));  // open: gt, lt
  Multiplexer #(.disabled("Z"), .enable("true"), .select(3), .width(64)) multiplexer_7 (
    .in0(bit_extender_5_out), .in1(bit_extender_6_out), .in2(multiplier_1_cout), .in3(multiplier_2_cout),
    .out(I), .sel(Op[2:0]), .en(Family2));  // open: in4, in5, in6, in7
  not not_9 (not_9_out, comparator_4_eq);
  Adder #(.width(64)) adder_1 (.a(A), .b(B), .out(adder_1_out), .cin(not_9_out), .cout(adder_1_cout));
  assign bit_extender_5_out = {{63{1'b0}}, adder_1_cout};  // Bit_Extender bit_extender_5
  assign bit_extender_6_out = {{63{1'b0}}, subtractor_1_bout};  // Bit_Extender bit_extender_6
  Subtractor #(.width(64)) subtractor_1 (
    .a(A), .b(B), .out(subtractor_1_out), .bin(not_9_out), .bout(subtractor_1_bout));
  Multiplier #(.width(64)) multiplier_1 (.a(A), .b(B), .out(multiplier_1_out), .cin(C), .cout(multiplier_1_cout));
  Multiplier #(.width(64)) multiplier_2 (.a(A), .b(B), .out(multiplier_2_out), .cin(C), .cout(multiplier_2_cout));
  Multiplexer #(.disabled("Z"), .width(64)) multiplexer_8 (.in0(A), .in1(B), .out(multiplexer_8_out), .sel(not_9_out));
  Multiplexer #(.disabled("Z"), .enable("true"), .select(3), .width(64)) multiplexer_9 (
    .in0(A), .in1(C), .out(O), .sel(Op[2:0]), .en(Family6));  // open: in2, in3, in4, in5, in6, in7
  Multiplexer #(.disabled("Z"), .enable("true"), .select(3), .width(64)) multiplexer_10 (
    .in0(A), .in1(C), .out(I), .sel(Op[2:0]), .en(Family6));  // open: in2, in3, in4, in5, in6, in7

  // Other names for the same wires on the sheet: OpLow[2:0] = Op[2:0]
endmodule

module RegFile (
  input  [4:0] WriteReg,
  input  WriteEnable,
  input  [63:0] Data,
  input  [4:0] Read0Reg,
  input  [4:0] Read1Reg,
  input  RIPOverride,
  input  [63:0] RIPData,
  input  Clock,
  input  Reset,
  output [63:0] Read0Data,
  output [63:0] Read1Data,
  output [63:0] RIP
);

  wire or_1_out, Sel0, Sel1, Sel2, Sel3, Sel4, Sel5, Sel6, Sel7, Sel8, Sel9, Sel10, Sel11, Sel12, Sel13,
       Sel14, Sel15, Sel16, Sel17, Sel18, Sel19, Sel20, Sel21, Sel22, Sel23, Sel24, Sel25, Sel26, Sel27,
       Sel28, Sel29, Sel30, Sel31;
  wire [63:0] multiplexer_1_out, Reg1, Reg2, Reg3, Reg4, Reg5, Reg6, Reg7, Reg8, Reg9, Reg10, Reg11, Reg12,
       Reg13, Reg14, Reg15, Reg16, Reg17, Reg18, Reg19, Reg20, Reg21, Reg22, Reg23, Reg24, Reg25, Reg26,
       Reg27, Reg28, Reg29, Reg30;

  Demultiplexer #(.select(5)) demultiplexer_1 (
    .out0(Sel0), .out1(Sel1), .out2(Sel2), .out3(Sel3), .out4(Sel4), .out5(Sel5), .out6(Sel6), .out7(Sel7),
    .out8(Sel8), .out9(Sel9), .out10(Sel10), .out11(Sel11), .out12(Sel12), .out13(Sel13), .out14(Sel14),
    .out15(Sel15), .out16(Sel16), .out17(Sel17), .out18(Sel18), .out19(Sel19), .out20(Sel20), .out21(Sel21),
    .out22(Sel22), .out23(Sel23), .out24(Sel24), .out25(Sel25), .out26(Sel26), .out27(Sel27), .out28(Sel28),
    .out29(Sel29), .out30(Sel30), .out31(Sel31), .in(WriteEnable), .sel(WriteReg));
  Multiplexer #(.disabled("Z"), .width(64)) multiplexer_1 (
    .in0(Data), .in1(RIPData), .out(multiplexer_1_out), .sel(RIPOverride));
  or or_1 (or_1_out, RIPOverride, Sel31);
  Register #(.width(64)) register_1 (.D(Data), .en(Sel1), .clk(Clock), .Q(Reg1), .clr(Reset));
  Register #(.width(64)) register_2 (.D(Data), .en(Sel2), .clk(Clock), .Q(Reg2), .clr(Reset));
  Register #(.width(64)) register_3 (.D(Data), .en(Sel3), .clk(Clock), .Q(Reg3), .clr(Reset));
  Register #(.width(64)) register_4 (.D(Data), .en(Sel4), .clk(Clock), .Q(Reg4), .clr(Reset));
  Register #(.width(64)) register_5 (.D(Data), .en(Sel5), .clk(Clock), .Q(Reg5), .clr(Reset));
  Register #(.width(64)) register_6 (.D(Data), .en(Sel6), .clk(Clock), .Q(Reg6), .clr(Reset));
  Register #(.width(64)) register_7 (.D(Data), .en(Sel7), .clk(Clock), .Q(Reg7), .clr(Reset));
  Register #(.width(64)) register_8 (.D(Data), .en(Sel8), .clk(Clock), .Q(Reg8), .clr(Reset));
  Register #(.width(64)) register_9 (.D(Data), .en(Sel9), .clk(Clock), .Q(Reg9), .clr(Reset));
  Register #(.width(64)) register_10 (.D(Data), .en(Sel10), .clk(Clock), .Q(Reg10), .clr(Reset));
  Register #(.width(64)) register_11 (.D(Data), .en(Sel11), .clk(Clock), .Q(Reg11), .clr(Reset));
  Register #(.width(64)) register_12 (.D(Data), .en(Sel12), .clk(Clock), .Q(Reg12), .clr(Reset));
  Register #(.width(64)) register_13 (.D(Data), .en(Sel13), .clk(Clock), .Q(Reg13), .clr(Reset));
  Register #(.width(64)) register_14 (.D(Data), .en(Sel14), .clk(Clock), .Q(Reg14), .clr(Reset));
  Register #(.width(64)) register_15 (.D(Data), .en(Sel15), .clk(Clock), .Q(Reg15), .clr(Reset));
  Register #(.width(64)) register_16 (.D(Data), .en(Sel16), .clk(Clock), .Q(Reg16), .clr(Reset));
  Register #(.width(64)) register_17 (.D(Data), .en(Sel17), .clk(Clock), .Q(Reg17), .clr(Reset));
  Register #(.width(64)) register_18 (.D(Data), .en(Sel18), .clk(Clock), .Q(Reg18), .clr(Reset));
  Register #(.width(64)) register_19 (.D(Data), .en(Sel19), .clk(Clock), .Q(Reg19), .clr(Reset));
  Register #(.width(64)) register_20 (.D(Data), .en(Sel20), .clk(Clock), .Q(Reg20), .clr(Reset));
  Register #(.width(64)) register_21 (.D(Data), .en(Sel21), .clk(Clock), .Q(Reg21), .clr(Reset));
  Register #(.width(64)) register_22 (.D(Data), .en(Sel22), .clk(Clock), .Q(Reg22), .clr(Reset));
  Register #(.width(64)) register_23 (.D(Data), .en(Sel23), .clk(Clock), .Q(Reg23), .clr(Reset));
  Register #(.width(64)) register_24 (.D(Data), .en(Sel24), .clk(Clock), .Q(Reg24), .clr(Reset));
  Register #(.width(64)) register_25 (.D(Data), .en(Sel25), .clk(Clock), .Q(Reg25), .clr(Reset));
  Register #(.width(64)) register_26 (.D(Data), .en(Sel26), .clk(Clock), .Q(Reg26), .clr(Reset));
  Register #(.width(64)) register_27 (.D(Data), .en(Sel27), .clk(Clock), .Q(Reg27), .clr(Reset));
  Register #(.width(64)) register_28 (.D(Data), .en(Sel28), .clk(Clock), .Q(Reg28), .clr(Reset));
  Register #(.width(64)) register_29 (.D(Data), .en(Sel29), .clk(Clock), .Q(Reg29), .clr(Reset));
  Register #(.width(64)) register_30 (.D(Data), .en(Sel30), .clk(Clock), .Q(Reg30), .clr(Reset));
  Register #(.width(64)) register_31 (.D(multiplexer_1_out), .en(or_1_out), .clk(Clock), .Q(RIP), .clr(Reset));
  Multiplexer #(.select(5), .width(64)) multiplexer_2 (
    .in0({64{1'b0}}), .in1(Reg1), .in2(Reg2), .in3(Reg3), .in4(Reg4), .in5(Reg5), .in6(Reg6), .in7(Reg7),
    .in8(Reg8), .in9(Reg9), .in10(Reg10), .in11(Reg11), .in12(Reg12), .in13(Reg13), .in14(Reg14),
    .in15(Reg15), .in16(Reg16), .in17(Reg17), .in18(Reg18), .in19(Reg19), .in20(Reg20), .in21(Reg21),
    .in22(Reg22), .in23(Reg23), .in24(Reg24), .in25(Reg25), .in26(Reg26), .in27(Reg27), .in28(Reg28),
    .in29(Reg29), .in30(Reg30), .in31(RIP), .out(Read0Data), .sel(Read0Reg));
  Multiplexer #(.select(5), .width(64)) multiplexer_3 (
    .in0({64{1'b0}}), .in1(Reg1), .in2(Reg2), .in3(Reg3), .in4(Reg4), .in5(Reg5), .in6(Reg6), .in7(Reg7),
    .in8(Reg8), .in9(Reg9), .in10(Reg10), .in11(Reg11), .in12(Reg12), .in13(Reg13), .in14(Reg14),
    .in15(Reg15), .in16(Reg16), .in17(Reg17), .in18(Reg18), .in19(Reg19), .in20(Reg20), .in21(Reg21),
    .in22(Reg22), .in23(Reg23), .in24(Reg24), .in25(Reg25), .in26(Reg26), .in27(Reg27), .in28(Reg28),
    .in29(Reg29), .in30(Reg30), .in31(RIP), .out(Read1Data), .sel(Read1Reg));

  // Other names for the same wires on the sheet: Reg31[63:0] = RIP
endmodule

module ALUDriver (
  input  [5:0] InstructionALUOp,
  input  [1:0] InstructionFlagsMode,
  input  [63:0] Reg0,
  input  [63:0] Reg1,
  input  [63:0] Immediate,
  input  [1:0] Mode,
  input  OverrideALU,
  input  [5:0] ALUOverrideValue,
  input  OverrideFlagsMode,
  input  [1:0] FlagsModeOverride,
  output [5:0] ALUOp,
  output [63:0] A,
  output [63:0] B,
  output WriteFlags,
  output ReadFlags
);

  wire decoder_1_out1, decoder_1_out2;

  Decoder #(.enable("false"), .select(2)) decoder_1 (
    .out1(decoder_1_out1), .out2(decoder_1_out2), .sel(Mode));  // open: out0, out3
  Multiplexer #(.disabled("Z"), .width(64)) multiplexer_1 (.in0(Reg0), .in1(Immediate), .out(A), .sel(decoder_1_out1));
  Multiplexer #(.disabled("Z"), .width(64)) multiplexer_2 (.in0(Reg1), .in1(Immediate), .out(B), .sel(decoder_1_out2));
  Multiplexer #(.width(6)) multiplexer_3 (
    .in0(InstructionALUOp), .in1(ALUOverrideValue), .out(ALUOp), .sel(OverrideALU));
  Multiplexer #(.width(2)) multiplexer_4 (
    .in0(InstructionFlagsMode), .in1(FlagsModeOverride), .out({ReadFlags, WriteFlags}),
    .sel(OverrideFlagsMode));
endmodule

module InstructionDecoder (
  input  [63:0] InstructionWord,
  output [63:0] InstructionSize,
  output [7:0] Opcode,
  output [4:0] A,
  output [4:0] B,
  output [4:0] D,
  output [5:0] ALUOp,
  output [1:0] FlagsMode,
  output [63:0] Immediate,
  output [1:0] Scale,
  output [1:0] Size
);

  wire byteinstructiondecoder_1_isbyteinstruction, doubleinstructiondecoder_1_isdoubleinstruction,
       quadinstructiondecoder_1_isquadinstruction;
  wire [1:0] controlled_buffer_1_out, quadinstructiondecoder_1_flagsmode, quadinstructiondecoder_1_scale,
       quadinstructiondecoder_1_size;
  wire [4:0] byteinstructiondecoder_1_rega, doubleinstructiondecoder_1_a, doubleinstructiondecoder_1_b,
       quadinstructiondecoder_1_a, quadinstructiondecoder_1_b, quadinstructiondecoder_1_d;
  wire [5:0] doubleinstructiondecoder_1_aluop, quadinstructiondecoder_1_aluop;
  wire [7:0] byteinstructiondecoder_1_opcode, doubleinstructiondecoder_1_opcode,
       quadinstructiondecoder_1_opcode;
  wire [63:0] doubleinstructiondecoder_1_immediate, quadinstructiondecoder_1_immediate;

  ByteInstructionDecoder byteinstructiondecoder_1 (
    .InstructionWord(InstructionWord), .IsByteInstruction(byteinstructiondecoder_1_isbyteinstruction),
    .Opcode(byteinstructiondecoder_1_opcode), .RegA(byteinstructiondecoder_1_rega));
  DoubleInstructionDecoder doubleinstructiondecoder_1 (
    .InstructionWord(InstructionWord), .IsDoubleInstruction(doubleinstructiondecoder_1_isdoubleinstruction),
    .Opcode(doubleinstructiondecoder_1_opcode), .A(doubleinstructiondecoder_1_a),
    .B(doubleinstructiondecoder_1_b), .Immediate(doubleinstructiondecoder_1_immediate),
    .ALUOp(doubleinstructiondecoder_1_aluop));
  QuadInstructionDecoder quadinstructiondecoder_1 (
    .InstructionWord(InstructionWord), .IsQuadInstruction(quadinstructiondecoder_1_isquadinstruction),
    .Opcode(quadinstructiondecoder_1_opcode), .A(quadinstructiondecoder_1_a), .B(quadinstructiondecoder_1_b),
    .D(quadinstructiondecoder_1_d), .Immediate(quadinstructiondecoder_1_immediate),
    .ALUOp(quadinstructiondecoder_1_aluop), .FlagsMode(quadinstructiondecoder_1_flagsmode),
    .Scale(quadinstructiondecoder_1_scale), .Size(quadinstructiondecoder_1_size));
  assign controlled_buffer_1_out = byteinstructiondecoder_1_isbyteinstruction ? 2'b00 : 2'bz;  // Controlled_Buffer controlled_buffer_1
  assign controlled_buffer_1_out = doubleinstructiondecoder_1_isdoubleinstruction ? 2'b01 : 2'bz;  // Controlled_Buffer controlled_buffer_2
  assign controlled_buffer_1_out = quadinstructiondecoder_1_isquadinstruction ? 2'b10 : 2'bz;  // Controlled_Buffer controlled_buffer_3
  Multiplexer #(.select(2), .width(64)) multiplexer_1 (
    .in0(64'h1), .in1(64'h2), .in3(64'h4), .out(InstructionSize), .sel(controlled_buffer_1_out));  // open: in2
  Multiplexer #(.select(2), .width(8)) multiplexer_2 (
    .in0(byteinstructiondecoder_1_opcode), .in1(doubleinstructiondecoder_1_opcode),
    .in2(quadinstructiondecoder_1_opcode), .out(Opcode), .sel(controlled_buffer_1_out));  // open: in3
  Multiplexer #(.select(2), .width(5)) multiplexer_3 (
    .in0(byteinstructiondecoder_1_rega), .in1(doubleinstructiondecoder_1_a),
    .in2(quadinstructiondecoder_1_a), .out(A), .sel(controlled_buffer_1_out));  // open: in3
  Multiplexer #(.select(2), .width(5)) multiplexer_4 (
    .in0({5{1'b0}}), .in1(doubleinstructiondecoder_1_b), .in2(quadinstructiondecoder_1_b), .out(B),
    .sel(controlled_buffer_1_out));  // open: in3
  Multiplexer #(.select(2), .width(5)) multiplexer_5 (
    .in0({5{1'b0}}), .in1({5{1'b0}}), .in2(quadinstructiondecoder_1_d), .out(D), .sel(controlled_buffer_1_out));  // open: in3
  Multiplexer #(.select(2), .width(6)) multiplexer_6 (
    .in0({6{1'b0}}), .in1(doubleinstructiondecoder_1_aluop), .in2(quadinstructiondecoder_1_aluop),
    .out(ALUOp), .sel(controlled_buffer_1_out));  // open: in3
  Multiplexer #(.select(2), .width(2)) multiplexer_7 (
    .in0(2'b00), .in1(2'b00), .in2(quadinstructiondecoder_1_flagsmode), .out(FlagsMode),
    .sel(controlled_buffer_1_out));  // open: in3
  Multiplexer #(.select(2), .width(64)) multiplexer_8 (
    .in0({64{1'b0}}), .in1(doubleinstructiondecoder_1_immediate), .in2(quadinstructiondecoder_1_immediate),
    .out(Immediate), .sel(controlled_buffer_1_out));  // open: in3
  Multiplexer #(.select(2), .width(2)) multiplexer_9 (
    .in0(2'b00), .in1(2'b00), .in2(quadinstructiondecoder_1_scale), .out(Scale), .sel(controlled_buffer_1_out));  // open: in3
  Multiplexer #(.select(2), .width(2)) multiplexer_10 (
    .in0(2'b00), .in1(2'b00), .in2(quadinstructiondecoder_1_size), .out(Size), .sel(controlled_buffer_1_out));  // open: in3
endmodule

module ByteInstructionDecoder (
  input  [63:0] InstructionWord,
  output IsByteInstruction,
  output [7:0] Opcode,
  output [4:0] RegA
);

  wire [1:0] pla_1_out;
  wire [7:0] bit_extender_1_out;

  Bit_Extender #(.in_width(64), .out_width(8), .\type ("zero")) bit_extender_1 (
    .in(InstructionWord), .out(bit_extender_1_out));
  PLA #(.in_width(8), .\table ("00000000 00 # NOP\n000xxxxx 01 # ZERO\n001xxxxx 10 # LFLAGS\n010xxxxx 11 # SFLAGS")) pla_1 (
    .in(bit_extender_1_out), .out(pla_1_out));
  Bit_Extender #(.out_width(5), .\type ("zero")) bit_extender_2 (.in(bit_extender_1_out), .out(RegA));
  not not_1 (IsByteInstruction, bit_extender_1_out[7]);
  assign Opcode = {{6{1'b0}}, pla_1_out};  // Bit_Extender bit_extender_3
endmodule

module DoubleInstructionDecoder (
  input  [63:0] InstructionWord,
  output IsDoubleInstruction,
  output [7:0] Opcode,
  output [4:0] A,
  output [4:0] B,
  output [63:0] Immediate,
  output [5:0] ALUOp
);

  wire comparator_1_eq, not_1_out;
  wire [3:0] pla_1_out;
  wire [5:0] bit_extender_4_out, multiplexer_1_out;
  wire [7:0] bit_extender_2_out;
  wire [7:2] bit_extender_1_out;

  Bit_Extender #(.in_width(64), .\type ("zero")) bit_extender_1 (
    .in(InstructionWord), .out({A[4:2], B, bit_extender_1_out, A[1:0]}));
  PLA #(.in_width(16), .out_width(4), .\table ("000xxxxx10000000 0000 # TEN\nxxx00000100000xx 0001 # TNN\nxxxxxxxx100000xx 0010 # MOV\nxxxxxxxx100xxxxx 0011 # ALU\n000xxxxx10100000 0100 # TEZ\n000xxxxx10100100 0101 # TNZ\nxxxxxxxx10100xxx 0110 # UNO\nxxxxxxxx101010xx 0111 # ADD\nxxxxxxxx101011xx 1000 # SUB\nxxxxxxxx101100xx 1001 # MUL")) pla_1 (
    .in({A[4:2], B, bit_extender_1_out, A[1:0]}), .out(pla_1_out));
  and and_1 (IsDoubleInstruction, ~bit_extender_1_out[6], bit_extender_1_out[7]);  // AND_Gate
  assign bit_extender_2_out = {{4{1'b0}}, pla_1_out};  // Bit_Extender bit_extender_2
  assign Opcode = bit_extender_2_out | 8'h40;  // OR_Gate or_1, 8 bits wide
  assign Immediate = {{59{B[4]}}, B};  // Bit_Extender bit_extender_3
  Multiplexer #(.disabled("Z"), .select(3), .width(6)) multiplexer_1 (
    .in1(6'b001000), .in2(6'b001001), .in3(6'b001010), .in4(6'b001011), .in5(6'b001100), .in6(6'b010000),
    .in7(6'b010001), .out(multiplexer_1_out), .sel(bit_extender_1_out[4:2]));  // open: in0
  assign bit_extender_4_out = {{5{bit_extender_1_out[2]}}, bit_extender_1_out[2]};  // Bit_Extender bit_extender_4
  Comparator #(.mode("unsigned")) comparator_1 (.a(Opcode), .b(8'h43), .eq(comparator_1_eq));  // open: gt, lt
  assign ALUOp = not_1_out ? bit_extender_4_out : 6'bz;  // Controlled_Buffer controlled_buffer_1
  assign ALUOp = comparator_1_eq ? multiplexer_1_out : 6'bz;  // Controlled_Buffer controlled_buffer_2
  not not_1 (not_1_out, comparator_1_eq);
endmodule

module QuadInstructionDecoder (
  input  [63:0] InstructionWord,
  output IsQuadInstruction,
  output [7:0] Opcode,
  output [4:0] A,
  output [4:0] B,
  output [4:0] D,
  output [63:0] Immediate,
  output [5:0] ALUOp,
  output [1:0] FlagsMode,
  output [1:0] Scale,
  output [1:0] Size
);

  wire [2:0] bit_extender_5_out;
  wire [7:0] pla_1_out;
  wire [31:0] bit_extender_1_out;
  wire [63:0] bit_extender_2_out, bit_extender_3_out, bit_extender_4_out;

  Bit_Extender #(.in_width(64), .out_width(32), .\type ("zero")) bit_extender_1 (
    .in(InstructionWord), .out({bit_extender_1_out[31:26], A, B, FlagsMode, ALUOp, bit_extender_1_out[7:0]}));
  PLA #(.in_width(8), .out_width(8), .\table ("000000xx 00000000 # ALU0\n001xxxxx 00000001 # LOAD\n010xxxxx 00000010 # STORE\n011xxxxx 00000011 # LEA\n10xxxxxx 00000100 # ALU1\n11xxxxxx 00000101 # ALU2")) pla_1 (
    .in({bit_extender_1_out[31:26], A[4:3]}), .out(pla_1_out));
  and and_1 (IsQuadInstruction, ~bit_extender_1_out[5], bit_extender_1_out[6], bit_extender_1_out[7]);  // AND_Gate
  assign bit_extender_2_out = {{57{bit_extender_1_out[28]}}, {bit_extender_1_out[28:26], ALUOp[3:0]}};  // Bit_Extender bit_extender_2
  assign bit_extender_3_out = {{55{bit_extender_1_out[28]}}, {bit_extender_1_out[28:26], ALUOp}};  // Bit_Extender bit_extender_3
  assign bit_extender_4_out = {{55{bit_extender_1_out[29]}}, {bit_extender_1_out[29:26], B}};  // Bit_Extender bit_extender_4
  Bit_Extender #(.out_width(3), .\type ("zero")) bit_extender_5 (.in(pla_1_out), .out(bit_extender_5_out));
  assign Opcode = 8'h80 | pla_1_out;  // OR_Gate or_1, 8 bits wide
  Multiplexer #(.select(3), .width(64)) multiplexer_1 (
    .in0({64{1'b0}}), .in1(bit_extender_2_out), .in2(bit_extender_2_out), .in3(bit_extender_3_out),
    .in4(bit_extender_4_out), .in5({64{1'b0}}), .in6({64{1'b0}}), .in7({64{1'b0}}), .out(Immediate),
    .sel(bit_extender_5_out));
  Bit_Extender #(.in_width(32), .out_width(5), .\type ("zero")) bit_extender_6 (
    .in({bit_extender_1_out[31:26], A, B, FlagsMode, ALUOp, bit_extender_1_out[7:0]}), .out(D));

  assign Scale = FlagsMode;
  assign Size = ALUOp[5:4];
endmodule

module RegDriver (
  input  [4:0] A,
  input  [4:0] B,
  input  [4:0] D,
  input  [1:0] Src0Mode,
  input  [1:0] Src1Mode,
  input  [1:0] DstMode,
  output [4:0] Src0,
  output [4:0] Src1,
  output [4:0] Dst
);

  Multiplexer #(.select(2), .width(5)) multiplexer_1 (
    .in0(A), .in1(B), .in2(D), .in3({5{1'b0}}), .out(Src0), .sel(Src0Mode));
  Multiplexer #(.select(2), .width(5)) multiplexer_2 (
    .in0(A), .in1(B), .in2(D), .in3({5{1'b0}}), .out(Src1), .sel(Src1Mode));
  Multiplexer #(.select(2), .width(5)) multiplexer_3 (
    .in0(A), .in1(B), .in2(D), .in3({5{1'b0}}), .out(Dst), .sel(DstMode));
endmodule

module AddressUnit (
  input  [63:0] Base,
  input  [63:0] Index,
  input  [63:0] Immediate,
  input  [1:0] Scale,
  input  Latch,
  input  Clock,
  output [63:0] Address
);

  wire [5:0] bit_extender_1_out;
  wire [63:0] adder_1_out, adder_2_out, shifter_1_out;

  assign bit_extender_1_out = {{4{1'b0}}, Scale};  // Bit_Extender bit_extender_1
  Shifter #(.width(64)) shifter_1 (.in(Index), .\dist (bit_extender_1_out), .out(shifter_1_out));
  Adder #(.width(64)) adder_1 (.a(Base), .b(Immediate), .out(adder_1_out), .cin(1'b0));  // open: cout
  Adder #(.width(64)) adder_2 (.a(adder_1_out), .b(shifter_1_out), .out(adder_2_out), .cin(1'b0));  // open: cout
  Register #(.width(64)) register_1 (.D(adder_2_out), .en(Latch), .clk(Clock), .Q(Address));  // open: clr
endmodule

module Microcode (
  input  Enable,
  input  [7:0] Opcode,
  input  [1:0] Cycle,
  output [1:0] Src0Mode,
  output [1:0] Src1Mode,
  output [1:0] DstMode,
  output MemEnable,
  output MemWrite,
  output AddressLatch,
  output RegWrite,
  output [1:0] ImmediateMode,
  output OverrideALU,
  output [5:0] ALUOverride,
  output OverrideFlags,
  output [1:0] FlagsOverride,
  output StateReset,
  output [2:0] RegSrc
);

  wire [25:0] pla_1_out;

  PLA #(.in_width(10), .out_width(26), .\table ("0000000000 00010000000000000000000000 # NOP")) pla_1 (
    .in({Cycle, Opcode}), .out(pla_1_out));
  Multiplexer #(.width(26)) multiplexer_1 (
    .in0({26{1'b0}}), .in1(pla_1_out),
    .out({RegSrc, StateReset, FlagsOverride, OverrideFlags, ALUOverride, OverrideALU, ImmediateMode, RegWrite, AddressLatch, MemWrite, MemEnable, DstMode, Src1Mode, Src0Mode}),
    .sel(Enable));
endmodule
